// Logisim project hkcpu.circ as structural Verilog
module alu (
  input  CLK,
  input  RST,
  input  [7:0] A,
  input  [7:0] B,
  input  [2:0] AOP,
  input  AO,
  output [2:0] FLGO,
  output [7:0] BUSO
);

  wire not_1_out;
  wire [2:0] comparator_1_gt;
  wire [7:0] adder_1_out, divider_1_out, multiplexer_1_out, multiplier_1_out, subtractor_1_out;

  Comparator comparator_1 (.a(A), .b(B), .gt(comparator_1_gt[0]), .eq(comparator_1_gt[1]), .lt(comparator_1_gt[2]));
  Adder adder_1 (.a(A), .b(B), .out(adder_1_out));  // open: cin, cout
  Subtractor subtractor_1 (.a(A), .b(B), .out(subtractor_1_out));  // open: bin, bout
  Multiplier multiplier_1 (.a(A), .b(B), .out(multiplier_1_out));  // open: cin, cout
  Divider divider_1 (.a(A), .b(B), .out(divider_1_out));  // open: upper, rem
  Register #(.width(3)) register_1 (.D(comparator_1_gt), .Q(FLGO), .clk(CLK), .clr(RST));  // open: en
  assign BUSO = AO ? multiplexer_1_out : 8'bz;  // Controlled_Buffer controlled_buffer_1
  Multiplexer #(.enable("true"), .select(2), .width(8)) multiplexer_1 (
    .in0(adder_1_out), .in1(subtractor_1_out), .in2(multiplier_1_out), .in3(divider_1_out),
    .out(multiplexer_1_out), .sel(AOP[1:0]), .en(not_1_out));
  not not_1 (not_1_out, AOP[2]);
endmodule

module LogicClock (
  input  CLKI,
  input  HLT,
  output CLKO
);

  and and_1 (CLKO, CLKI, HLT);
endmodule

module LogicCounter (
  input  CLK,
  input  RST,
  input  [7:0] BUSI,
  input  CE,
  input  CO,
  input  CL,
  output [7:0] BUSO
);

  wire [7:0] counter_1_q;

  Counter counter_1 (.load(CL), .D(BUSI), .count(CE), .Q(counter_1_q), .clk(CLK), .clr(RST));  // open: carry, up
  assign BUSO = CO ? counter_1_q : 8'bz;  // Controlled_Buffer controlled_buffer_1
endmodule

module regs (
  input  CLK,
  input  RST,
  input  [7:0] BUSI,
  input  [2:0] RI,
  input  [2:0] RO,
  output [7:0] ABPS,
  output [7:0] BBPS,
  output [7:0] BUSO
);

  wire [7:0] register_3_q;

  Register register_1 (.D(BUSI), .en(RI[0]), .Q(ABPS), .clk(CLK), .clr(RST));
  Register register_2 (.D(BUSI), .en(RI[1]), .Q(BBPS), .clk(CLK), .clr(RST));
  Register register_3 (.D(BUSI), .en(RI[2]), .Q(register_3_q), .clk(CLK), .clr(RST));
  assign BUSO = RO[0] ? ABPS : 8'bz;  // Controlled_Buffer controlled_buffer_1
  assign BUSO = RO[1] ? BBPS : 8'bz;  // Controlled_Buffer controlled_buffer_2
  assign BUSO = RO[2] ? register_3_q : 8'bz;  // Controlled_Buffer controlled_buffer_3
endmodule

module memory (
  input  CLK,
  input  RST,
  input  [7:0] BUSI,
  input  [7:0] CMDI,
  input  MAI,
  input  MI,
  input  MO,
  output [7:0] CMA,
  output CMI,
  output [7:0] CMDO,
  output [7:0] BUSO
);

  Register register_1 (.D(BUSI), .en(MAI), .Q(CMA), .clk(CLK), .clr(RST));
  assign BUSO = MO ? CMDI : 8'bz;  // Controlled_Buffer controlled_buffer_1

  assign CMDO = BUSI;
  assign CMI = MI;
endmodule

module LogicOutput (
  input  CLK,
  input  RST,
  input  [7:0] BUSI,
  input  OE,
  output [7:0] LogicOut
);

  Register register_1 (.D(BUSI), .en(OE), .Q(LogicOut), .clk(CLK), .clr(RST));
endmodule

module LogicControl (
  input  CLK,
  input  RST,
  input  [7:0] BUSI,
  input  [2:0] FLGI,
  input  IRI,
  input  ARI,
  input  ARO,
  output [21:0] LCO,
  output [7:0] BUSO
);

  wire [2:0] counter_1_q;
  wire [7:0] register_1_q, register_2_q;

  Counter #(.max('h7), .trigger("falling"), .width(3)) counter_1 (
    .Q(counter_1_q), .clk(CLK), .clr(RST));  // open: load, D, count, carry, up
  Register register_1 (.D(BUSI), .en(IRI), .Q(register_1_q), .clk(CLK), .clr(RST));
  assign BUSO = ARO ? register_2_q : 8'bz;  // Controlled_Buffer controlled_buffer_1
  Register register_2 (.D(BUSI), .en(ARI), .Q(register_2_q), .clk(CLK), .clr(RST));
  PLA #(.in_width(14), .out_width(22), .\table ("xxxxxxxxxxx000 0000001000000001000000\nxxxxxxxxxxx001 0000000100000000010100")) pla_1 (
    .in({register_1_q, FLGI, counter_1_q}), .out(LCO));
endmodule
